# Fritzing sketch weatherstation (saved by Fritzing 0.9.3b)
breadboards: 1

parts:
  Raspberry_Pi1 = Raspberry Pi 2
  Part1 = Barometric Pressure Sensor - BMP180 Breakout (GY-68)
  RHT1 = Humidity and Temperature Sensor RHT03

nets:
  3V3: Raspberry_Pi1.3v3, Raspberry_Pi1.3V3, Part1.VCC, RHT1.Vcc
  N1: Raspberry_Pi1.GPIO2, Part1.SDA
  N2: Raspberry_Pi1.GPIO3, Part1.SCL
  N3: Raspberry_Pi1.GPIO4, RHT1.Data-signal
  GND: Raspberry_Pi1.GND, Part1.GND, RHT1.GND_2
